// Logisim project Calculadora Binária.circ as structural Verilog: 3 circuits, main circuit MeioSomador
module MeioSomador (
  input  A,
  input  B,
  output S,
  output Co
);

  and and_1 (Co, A, B);
  xor xor_1 (S, A, B);
endmodule

module Somador (
  input  A,
  input  B,
  input  CI,
  output s,
  output CO
);

  wire meiosomador_1_co, meiosomador_1_s, meiosomador_2_co;

  MeioSomador meiosomador_1 (.A(A), .B(B), .S(meiosomador_1_s), .Co(meiosomador_1_co));
  MeioSomador meiosomador_2 (.A(CI), .B(meiosomador_1_s), .S(s), .Co(meiosomador_2_co));
  or or_1 (CO, meiosomador_1_co, meiosomador_2_co);
endmodule

module Somador2Bits (
  input  A0,
  input  B0,
  input  A1,
  input  B1,
  output S0,
  output S1,
  output Co
);

  wire somador_1_co;

  Somador somador_1 (.A(A0), .B(B0), .CI(1'b0), .s(S0), .CO(somador_1_co));
  Somador somador_2 (.A(A1), .B(B1), .CI(somador_1_co), .s(S1), .CO(Co));
endmodule
